# Fritzing sketch robo (saved by Fritzing 0.9.6b)
breadboards: 1

parts:
  Part1 = Arduino Uno (Rev3)
  Part2 = Color Sensor Breakout ADJD-S311
  HC-SR04_Sensor_1 = HC-SR04 Ultrasonic Distance Sensor
  M1 = Dagu DGServo 9g (Pan and tilt) [part_number=RS001B]
  M2 = Dagu DGServo 9g (Pan and tilt) [part_number=RS001B]
  M3 = Dagu DGServo 9g (Pan and tilt) [part_number=RS001B]
  M4 = Dagu DGServo 9g (Pan and tilt) [part_number=RS001B]
  U1 = L298 [package=multiwatt15_6400bgheatsink]
  M5 = gear-motor
  M6 = gear-motor

nets:
  N1: Part1.A4/SDA, Part2.SDA
  N2: Part1.A5/SCL, Part2.SCL
  N3: Part1.D8, M3.pulse
  N4: Part1.D9_PWM, U1.ENA
  N5: Part1.D10_PWM/SS, U1.ENB
  N6: Part1.D11_PWM/MOSI, M4.pulse
  N7: Part1.D12/MISO, HC-SR04_Sensor_1.TRIG
  N8: Part1.D13/SCK, HC-SR04_Sensor_1.ECHO
  N9: Part1.D2, M2.pulse
  N10: Part1.D3_PWM, U1.IN1
  N11: Part1.D4, U1.IN2
  N12: Part1.D5_PWM, U1.IN3
  N13: Part1.D6_PWM, U1.IN4
  N14: Part1.D7, M1.pulse
  N15: U1.OUT1, M6.pin_2
  N16: U1.OUT2, M6.pin_1
  N17: U1.OUT3, M5.pin_2
  N18: U1.OUT4, M5.pin_1
